# Fritzing sketch strip_controller_board (saved by Fritzing 0.9.3b)
circuit board: 8.46667cm x 5.64444cm
breadboards: 1

parts:
  IC1 = IC, DIP package, 14 pins [chip_label=IC]
  J1 = female alternating pin header, 4 pins [form="♀ (female)"]
  Q1 = NPN-Transistor [package="TO92 [THT]"]
  Q2 = npn-Powertransistor [package="TO220 [THT]"]
  R1 = Resistor [tolerance=±5% resistance=1k package=THT]
  R2 = Resistor [tolerance=±5% resistance=1k package=THT]
  R3 = Resistor [tolerance=±5% resistance=1k package=THT]
  R4 = Resistor [tolerance=±5% resistance=10k package=THT]
  Q3 = NPN-Transistor [package="TO92 [THT]"]
  Q4 = NPN-Transistor [package="TO92 [THT]"]
  Q5 = npn-Powertransistor [package="TO220 [THT]"]
  Q6 = npn-Powertransistor [package="TO220 [THT]"]
  R5 = Resistor [tolerance=±5% resistance=10k package=THT]
  R6 = Resistor [tolerance=±5% resistance=10k package=THT]
  J2 = female alternating pin header, 4 pins [form="♀ (female)"]
  J3 = female pin header, 2 pins [form="♀ (female)"]
  J4 = female pin header, 2 pins [form="♀ (female)"]

nets:
  N1: IC1.pin1, J1.pin1, Q1.E, Q2.emitter, Q3.E, Q4.E, Q5.emitter, Q6.emitter, J4.pin1, J4.pin2
  N2: IC1.pin6, J1.pin2
  N3: IC1.pin7, R2.Pin_0
  N4: IC1.pin8, J1.pin3
  N5: IC1.pin9, R3.Pin_0
  N6: IC1.pin10, R1.Pin_0
  N7: IC1.pin11, IC1.pin14, J1.pin4
  N8: Q1.B, R1.Pin_1
  N9: Q1.C, Q2.base, R4.Pin_0, J2.pin4
  N10: Q2.collector, J2.pin3
  N11: R2.Pin_1, Q4.B
  N12: R3.Pin_1, Q3.B
  N13: R4.Pin_1, R5.Pin_1, R6.Pin_1, J3.pin1, J3.pin2
  N14: Q3.C, Q6.base, R5.Pin_0
  N15: Q4.C, Q5.base, R6.Pin_0
  N16: Q5.collector, J2.pin1
  N17: Q6.collector, J2.pin2
